# Fritzing sketch RGB_LED (saved by Fritzing 0.9.3b)
breadboards: 1

parts:
  R2 = Resistor [tolerance=±5% resistance=220 package=THT]
  R1 = Resistor [tolerance=±5% resistance=220 package=THT]
  LED = RGB LED (com. cathode, rgb) [package="5 mm [THT]"]
  Part3 = 5G_IoT_Hub
  R3 = Resistor [tolerance=±5% resistance=220 package=THT]

nets:
  N1: R2.Pin_0, LED.green_anode, Part3.MOSI
  N2: R2.Pin_1, R1.Pin_1, Part3.3V3, R3.Pin_1
  N3: R1.Pin_0, LED.blue_anode, Part3.SS
  N4: LED.red_anode, Part3.MISO, R3.Pin_0
  N5: LED.common_cathode, Part3.LED1, Part3.GND

custom parts:
  5G_IoT_Hub: 5G IoT Hub
