# Fritzing sketch Key_Switch (saved by Fritzing 0.9.3b)
breadboards: 1

parts:
  R3 = Resistor [tolerance=±5% resistance=220 package=THT]
  S1 = Pushbutton [package="[THT]"]
  S2 = Pushbutton [package="[THT]"]
  LED1 = LED - 5mm [color="Red (633nm)" package="5 mm [THT]"]
  Part2 = 5G_IoT_Hub

nets:
  N1: R3.Pin_0, LED1.cathode, Part2.SS
  N2: R3.Pin_1, Part2.3V3
  N3: S1.Pin_1, S1.Pin_2, S2.Pin_1, S2.Pin_2, LED1.anode, Part2.LED1, Part2.GND
  N4: S1.Pin_3, S1.Pin_4, Part2.PA6
  N5: S2.Pin_3, S2.Pin_4, Part2.PA7

custom parts:
  5G_IoT_Hub: 5G IoT Hub
