# Fritzing sketch active_buzzer (saved by Fritzing 0.9.3b)
breadboards: 1

parts:
  Part2 = KY-012 Active Buzzer Module [package="Breakout board"]
  Part5 = 5G_IoT_Hub

nets:
  N1: Part2.S, Part5.PA6
  N2: Part2.-, Part5.LED1, Part5.LED2, Part5.GND

custom parts:
  KY-012 Active Buzzer Module: Active Piezoelectric Buzzer Module Keyes KY-012, it produces single-tone sound when signal is high.
  5G_IoT_Hub: 5G IoT Hub
