# Fritzing sketch Analog_Joystick (saved by Fritzing 0.9.3b)

parts:
  Part1 = Adafruit Analog 2-Axis Joystick [part_number="Adafruit #512"]
  Part3 = 5G_IoT_Hub

nets:
  GND: Part1.GND, Part3.LED2, Part3.GND
  N1: Part1.SWITCH, Part3.PA6
  N2: Part1.YOUT, Part3.A1
  N3: Part1.XOUT, Part3.A0
  VCC: Part1.VCC, Part3.3V3

custom parts:
  Adafruit Analog 2-Axis Joystick: This mini-kit makes it easy to mount a PSP/Xbox-like thumb joystick to your project. The thumbstick is an analog joystick - more accurate and sensitive than just 'directional' joysticks - with a 'press in to select' button. Since it's analog, you'll need two analog reading pins on your microcontroller to determine X and Y. Having an extra digital input will let you read the switch. The pack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
  5G_IoT_Hub: 5G IoT Hub
