# Fritzing sketch IR_Receiver_Module (saved by Fritzing 0.9.3b)
breadboards: 1

parts:
  Part1 = IR Receiver Breakout [package=PCB]
  Part3 = 5G_IoT_Hub

nets:
  GND: Part1.GND, Part3.LED1, Part3.GND
  N1: Part1.OUT, Part3.MISO
  VCC: Part1.VCC, Part3.3V3

custom parts:
  5G_IoT_Hub: 5G IoT Hub
