# Fritzing sketch Water_level (saved by Fritzing 0.9.3b)

parts:
  Part3 = 5G_IoT_Hub
  Part4 = Water Sensor

nets:
  3V3: Part3.3V3, Part4.VCC
  GND: Part3.LED2, Part3.GND, Part4.GND
  N1: Part3.A0, Part4.SIG

custom parts:
  5G_IoT_Hub: 5G IoT Hub
  Water Sensor: SparkFun Soil Moisture Sensor The SparkFun Soil Moisture Sensor is a simple breakout for measuring the moisture in soil and similar materials. The soil moisture sensor is pretty straight forward to use. The two large exposed pads function as probes for the sensor, together acting as a variable resistor. The more water that is in the soil means the better the conductivity between the pads will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
