# Fritzing sketch DS1307 (saved by Fritzing 0.9.3b)
breadboards: 1

parts:
  Part1 = 5G_IoT_Hub
  IC1 = DS1307 [package=THT]

nets:
  N1: Part1.5V, IC1.+V
  N2: Part1.GND, IC1.0V
  N3: Part1.SDA, IC1.SDA_-_I2C_Data
  N4: Part1.SCL, IC1.SCL_-_I2C_Clock

custom parts:
  5G_IoT_Hub: 5G IoT Hub
