# Fritzing sketch Sound_Sensor (saved by Fritzing 0.9.3b)
breadboards: 1

parts:
  Mic1 = KY-038
  Part2 = 5G_IoT_Hub

nets:
  N1: Mic1.pin1, Part2.A0
  N2: Mic1.pin2, Part2.LED2
  N3: Mic1.pin3, Part2.3V3
  N4: Mic1.pin4, Part2.PA6

custom parts:
  KY-038: ky-038 Microphone sound sensor module
  5G_IoT_Hub: 5G IoT Hub
