# Fritzing sketch MF-RC522_RFID (saved by Fritzing 0.9.3b)

parts:
  Part2 = RFID-RC522-v3
  Part3 = 5G_IoT_Hub

nets:
  N1: Part2.SDA, Part3.SS
  N2: Part2.SCK, Part3.SCK
  N3: Part2.MOSI, Part3.MOSI
  N4: Part2.MISO, Part3.MISO
  GND: Part2.GND, Part3.LED1, Part3.GND
  N5: Part2.RST, Part3.PA6
  3.3V: Part2.3.3V, Part3.3V3

custom parts:
  RFID-RC522-v3: A simple China made RFID-RC522 Reader (6x4 cm); do check the pin labels, as this is a MFRC522 based clone.
  5G_IoT_Hub: 5G IoT Hub
