# Fritzing sketch LCD_display (saved by Fritzing 0.9.3b)
breadboards: 1

parts:
  U1 = LCD-16X2 [package=lcd-16x2_noholes]
  R1 = Trimmer Potentiometer [maximum_resistance=10kΩ package=THT]
  Part2 = 5G_IoT_Hub

nets:
  N1: U1.VSS, U1.R_W, R1.leg1, Part2.LED1
  VDD: U1.VDD, R1.leg2, Part2.5V
  N2: U1.VO, R1.wiper
  N3: U1.RS, Part2.PA6
  N4: U1.E, Part2.PA7
  N5: U1.DB4, Part2.SS
  N6: U1.DB5, Part2.MOSI
  N7: U1.DB6, Part2.MISO
  N8: U1.DB7, Part2.SCK

custom parts:
  5G_IoT_Hub: 5G IoT Hub
