# Fritzing sketch Photocell (saved by Fritzing 0.9.3b)
breadboards: 1

parts:
  IC1 = SHIFT REGISTER [package=dil16]
  R7 = Resistor [tolerance=±5% resistance=220 package=THT]
  R6 = Resistor [tolerance=±5% resistance=220 package=THT]
  R5 = Resistor [tolerance=±5% resistance=220 package=THT]
  R4 = Resistor [tolerance=±5% resistance=220 package=THT]
  LED1 = LED - 5mm [color="Red (633nm)" package="5 mm [THT]"]
  LED2 = LED - 5mm [color="Red (633nm)" package="5 mm [THT]"]
  LED3 = LED - 5mm [color="Red (633nm)" package="5 mm [THT]"]
  LED4 = LED - 5mm [color="Red (633nm)" package="5 mm [THT]"]
  LED5 = LED - 5mm [color="Red (633nm)" package="5 mm [THT]"]
  LED6 = LED - 5mm [color="Red (633nm)" package="5 mm [THT]"]
  LED7 = LED - 5mm [color="Red (633nm)" package="5 mm [THT]"]
  LED8 = LED - 5mm [color="Red (633nm)" package="5 mm [THT]"]
  R9 = PHOTOCELL [package=photocell]
  R10 = Resistor [tolerance=±5% resistance=1k package=THT]
  Part2 = 5G_IoT_Hub
  R11 = Resistor [tolerance=±5% resistance=220 package=THT]
  R12 = Resistor [tolerance=±5% resistance=220 package=THT]
  R13 = Resistor [tolerance=±5% resistance=220 package=THT]
  R14 = Resistor [tolerance=±5% resistance=220 package=THT]

nets:
  N1: IC1.QB, R13.Pin_0
  N2: IC1.QC, R12.Pin_0
  N3: IC1.QD, R4.Pin_0
  N4: IC1.QE, R5.Pin_0
  N5: IC1.QF, R6.Pin_0
  N6: IC1.QG, R7.Pin_0
  N7: IC1.QH, R11.Pin_0
  GND: IC1.GND, IC1.G, LED1.cathode, LED2.cathode, LED3.cathode, LED4.cathode, LED5.cathode, LED6.cathode, LED7.cathode, LED8.cathode, R10.Pin_1, Part2.LED1, Part2.GND
  VCC: IC1.SCL, IC1.VCC, Part2.5V
  N8: IC1.SCK, Part2.SS
  N9: IC1.RCK, Part2.PA7
  N10: IC1.SER, Part2.PA6
  N11: IC1.QA, R14.Pin_0
  N12: R7.Pin_1, LED7.anode
  N13: R6.Pin_1, LED6.anode
  N14: R5.Pin_1, LED5.anode
  N15: R4.Pin_1, LED4.anode
  N16: LED1.anode, R14.Pin_1
  N17: LED2.anode, R13.Pin_1
  N18: LED3.anode, R12.Pin_1
  N19: LED8.anode, R11.Pin_1
  N20: R9.P$1, Part2.3V3
  N21: R9.P$2, R10.Pin_0, Part2.A0

custom parts:
  5G_IoT_Hub: 5G IoT Hub
