# Fritzing sketch 7 segment (saved by Fritzing 0.9.3b)
breadboards: 1

parts:
  IC1 = SHIFT REGISTER [package=dil16]
  7_Segment = 7 Segment Display
  R1 = Resistor [tolerance=±5% resistance=220 package=THT]
  R8 = Resistor [tolerance=±5% resistance=220 package=THT]
  R3 = Resistor [tolerance=±5% resistance=220 package=THT]
  R7 = Resistor [tolerance=±5% resistance=220 package=THT]
  R6 = Resistor [tolerance=±5% resistance=220 package=THT]
  R5 = Resistor [tolerance=±5% resistance=220 package=THT]
  R4 = Resistor [tolerance=±5% resistance=220 package=THT]
  Part2 = 5G_IoT_Hub
  R2 = Resistor [tolerance=±5% resistance=220 package="0402 [SMD]"]

nets:
  N1: IC1.QB, R2.Pin_1
  N2: IC1.QC, R3.Pin_1
  N3: IC1.QD, R4.Pin_0
  N4: IC1.QE, R5.Pin_0
  N5: IC1.QF, R6.Pin_0
  N6: IC1.QG, R7.Pin_0
  N7: IC1.QH, R8.Pin_1
  GND: IC1.GND, IC1.G, 7_Segment.common_cathode, Part2.LED2, Part2.GND
  VCC: IC1.SCL, IC1.VCC, Part2.5V
  N8: IC1.SCK, Part2.SS
  N9: IC1.RCK, Part2.PA7
  N10: IC1.SER, Part2.PA6
  N11: IC1.QA, R1.Pin_1
  N12: 7_Segment.Segment_E, R5.Pin_1
  N13: 7_Segment.Segment_D, R4.Pin_1
  N14: 7_Segment.Segment_C, R3.Pin_0
  N15: 7_Segment.Segment_DP, R8.Pin_0
  N16: 7_Segment.Segment_B, R2.Pin_0
  N17: 7_Segment.Segment_A, R1.Pin_0
  N18: 7_Segment.Segment_F, R6.Pin_1
  N19: 7_Segment.Segment_G, R7.Pin_1

custom parts:
  5G_IoT_Hub: 5G IoT Hub
