# Fritzing sketch Relay (saved by Fritzing 0.9.3b)

parts:
  Part2 = KY-019 5V Relay Module [package="Breakout board"]
  M1 = DC Motor
  J1 = Power Jack [package=power_jack_combo]
  Part3 = 5G_IoT_Hub

nets:
  N1: Part2.S, Part3.PA7
  N2: Part2.+, Part3.5V
  N3: Part2.-, Part3.LED1, Part3.LED2, Part3.GND
  N4: Part2.Common, J1.GND
  N5: Part2.NO, M1.pin_2
  N6: M1.pin_1, J1.PWR

custom parts:
  KY-019 5V Relay Module: KY-019 5V Relay module, used to control AC circuits.
  5G_IoT_Hub: 5G IoT Hub
