# Fritzing sketch stepper (saved by Fritzing 0.9.3b)
breadboards: 1

parts:
  ULN2003 = Darlington Driver [package=so18l]
  MOTOR1 = Adafruit Gear-Reduced Stepper Motor (small)
  Part2 = 5G_IoT_Hub

nets:
  N1: ULN2003.1, Part2.PA6
  N2: ULN2003.2, Part2.PA7
  N3: ULN2003.3, Part2.SS
  N4: ULN2003.4, Part2.MOSI
  N5: ULN2003.9, Part2.LED1
  N6: ULN2003.10, MOTOR1.RED, Part2.5V
  N7: ULN2003.15, MOTOR1.ORANGE
  N8: ULN2003.16, MOTOR1.YELLOW
  N9: ULN2003.17, MOTOR1.PINK
  N10: ULN2003.18, MOTOR1.BLUE

custom parts:
  Adafruit Gear-Reduced Stepper Motor (small): Adafruit gear-reduction stepper motor (small)
  5G_IoT_Hub: 5G IoT Hub
