# Fritzing sketch With_Remote (saved by Fritzing 0.9.3b)
breadboards: 1

parts:
  ULN2003 = Darlington Driver [package=so18l]
  MOTOR1 = Adafruit Gear-Reduced Stepper Motor (small)
  Part2 = IR Receiver Breakout [package=PCB]
  Part3 = 5G_IoT_Hub

nets:
  N1: ULN2003.1, Part3.PA6
  N2: ULN2003.2, Part3.PA7
  N3: ULN2003.3, Part3.SS
  N4: ULN2003.4, Part3.MOSI
  GND: ULN2003.9, Part2.GND, Part3.LED1, Part3.GND
  N5: ULN2003.10, MOTOR1.RED, Part3.5V
  N6: ULN2003.15, MOTOR1.ORANGE
  N7: ULN2003.16, MOTOR1.YELLOW
  N8: ULN2003.17, MOTOR1.PINK
  N9: ULN2003.18, MOTOR1.BLUE
  N10: Part2.OUT, Part3.MISO
  VCC: Part2.VCC, Part3.3V3

custom parts:
  Adafruit Gear-Reduced Stepper Motor (small): Adafruit gear-reduction stepper motor (small)
  5G_IoT_Hub: 5G IoT Hub
