# Fritzing sketch passive_buzzer (saved by Fritzing 0.9.3b)
breadboards: 1

parts:
  Part3 = 5G_IoT_Hub
  J1 = Piezo Speaker

nets:
  N1: Part3.LED2, Part3.GND, J1.pin2
  N2: Part3.PA6, J1.pin1

custom parts:
  5G_IoT_Hub: 5G IoT Hub
