# Fritzing sketch Ball_Switch (saved by Fritzing 0.9.3b)
breadboards: 1

parts:
  S1 = Tilt Switch [package=THT]
  Part2 = 5G_IoT_Hub

nets:
  N1: S1.Pin_1, Part2.PA6
  N2: S1.Pin_2, Part2.LED2, Part2.GND

custom parts:
  5G_IoT_Hub: 5G IoT Hub
