# Fritzing sketch Servo (saved by Fritzing 0.9.3b)

parts:
  J1 = Basic Servo
  Part3 = 5G_IoT_Hub

nets:
  GND: J1.gnd, Part3.GND
  VCC: J1.vcc, Part3.5V
  N1: J1.pulse, Part3.PA7

custom parts:
  5G_IoT_Hub: 5G IoT Hub
