# Fritzing sketch Keypad (saved by Fritzing 0.9.3b)

parts:
  Keypad4x4 = Keypad Membran 4x4
  Part2 = 5G_IoT_Hub

nets:
  N1: Keypad4x4.Pin1, Part2.PA6
  N2: Keypad4x4.Pin2, Part2.PA7
  N3: Keypad4x4.Pin3, Part2.SS
  N4: Keypad4x4.Pin4, Part2.MOSI
  N5: Keypad4x4.Pin5, Part2.A0
  N6: Keypad4x4.Pin6, Part2.A1
  N7: Keypad4x4.Pin7, Part2.A2
  N8: Keypad4x4.Pin8, Part2.A3

custom parts:
  Keypad Membran 4x4: Membrane Keypad 4x4 Matrix
  5G_IoT_Hub: 5G IoT Hub
