# Fritzing sketch DHT11 (saved by Fritzing 0.9.3b)

parts:
  RHT1 = Humidity and Temperature Sensor RHT03
  Part2 = 5G_IoT_Hub

nets:
  VCC: RHT1.Vcc, Part2.3V3
  N1: RHT1.Data-signal, Part2.PA6
  N2: RHT1.GND_2, Part2.GND

custom parts:
  5G_IoT_Hub: 5G IoT Hub
